// Logisim project 8bit CPU.circ as structural Verilog: 7 circuits, main circuit main
// 8bit
module main (
  input  in_1,
  input  MODE,
  input  in_3,
  input  in_4,
  input  ADDRESS,
  input  in_6,
  input  in_7,
  input  in_8,
  input  in_9,
  input  in_10,
  input  in_11,
  input  Data,
  input  in_13,
  input  in_14,
  input  in_15,
  input  in_16,
  input  in_17,
  input  in_18,
  input  in_19,
  input  \ΣOUT ,
  input  \ΣIN ,
  input  A_out,
  input  B_out,
  input  C_out,
  input  D_out,
  input  RO,
  input  PCE,
  input  PC_OUT,
  input  IC_R,
  input  ADD_nSUB,
  input  A_In,
  input  B_In,
  input  C_In,
  input  D_In,
  input  RI,
  input  MAR_In,
  input  PC_IN,
  input  IR_IN,
  input  HLT,
  output BUS_HLD_IP
);

  wire A_q0, A_q1, A_q2, A_q3, A_q4, A_q5, A_q6, A_q7, and_1_out, and_2_out, and_3_out, and_4_out, and_5_out,
       and_6_out, and_7_out, and_8_out, and_9_out, and_10_out, and_11_out, and_12_out, and_13_out,
       and_14_out, and_15_out, and_16_out, and_17_out, and_18_out, button_1_out, button_2_out, button_3_out,
       clock_1_out, control_unit_1_a_in, control_unit_1_a_out, control_unit_1_add_nsub, control_unit_1_b_in,
       control_unit_1_b_out, control_unit_1_c_in, control_unit_1_c_out, control_unit_1_cf,
       control_unit_1_d_in, control_unit_1_d_out, control_unit_1_hlt, control_unit_1_ic_r,
       control_unit_1_inc, control_unit_1_ir_in, control_unit_1_mar_in, control_unit_1_pc_in,
       control_unit_1_pc_out, control_unit_1_pce, control_unit_1_ri, control_unit_1_ro, control_unit_1_zf,
       \control_unit_1_σin , \control_unit_1_σout , F_REG_q6, F_REG_q7, INSTRUCTION_REG_q0,
       INSTRUCTION_REG_q1, INSTRUCTION_REG_q2, INSTRUCTION_REG_q3, INSTRUCTION_REG_q4, INSTRUCTION_REG_q5,
       INSTRUCTION_REG_q6, INSTRUCTION_REG_q7, n74ls83_1_c4, \n74ls83_1_σ0 , \n74ls83_1_σ1 , \n74ls83_1_σ2 ,
       \n74ls83_1_σ3 , n74ls83_2_c4, \n74ls83_2_σ0 , \n74ls83_2_σ1 , \n74ls83_2_σ2 , \n74ls83_2_σ3 ,
       n74ls160_1_q0, n74ls160_1_q1, n74ls160_1_q2, n74ls160_1_q3, n74ls160_2_q0, n74ls160_2_q1,
       n74ls160_2_q2, n74ls160_2_q3, n74ls160_2_rco, n74ls160_3_q0, n74ls160_3_q1, n74ls160_3_q2,
       n74ls160_3_q3, nand_1_out, nand_2_out, nand_3_out, nand_4_out, nand_5_out, nand_6_out, nand_7_out,
       nand_8_out, nand_9_out, nand_10_out, nand_11_out, nand_12_out, nand_13_out, nand_14_out, nand_15_out,
       nand_16_out, nand_17_out, not_1_out, not_2_out, not_3_out, not_4_out, not_5_out, not_6_out, not_7_out,
       not_8_out, not_9_out, or_1_out, or_2_out, or_3_out, or_4_out, or_5_out, or_6_out, or_7_out, or_8_out,
       or_9_out, or_10_out, or_11_out, or_12_out, or_13_out, PGM_out, xor_1_out, xor_2_out, xor_3_out,
       xor_4_out, xor_5_out, xor_6_out, xor_7_out, xor_8_out, \Σ_REG_q0 , \Σ_REG_q1 , \Σ_REG_q2 , \Σ_REG_q3 ,
       \Σ_REG_q4 , \Σ_REG_q5 , \Σ_REG_q6 , \Σ_REG_q7 ;
  wire [3:0] n74ls245_2_q0, ssd_1_disp1, ssd_1_disp2, ssd_1_disp3;
  wire [7:0] n74ls245_1_q0, ram_1_data;
  wire [7:4] n74ls245_2_q4;

  Button button_1 (.out(button_1_out));
  or or_1 (or_1_out, button_2_out, button_1_out);
  or or_2 (or_2_out, control_unit_1_pc_in, or_3_out);
  or or_3 (or_3_out, and_1_out, and_2_out);
  and and_1 (and_1_out, control_unit_1_cf, F_REG_q6);
  _74LS574 F_REG (
    .D6(n74ls83_1_c4), .D7(not_1_out), .nOE(1'b0), .Q6(F_REG_q6), .Q7(F_REG_q7), .CP(and_3_out));  // open: D0, D1, D2, D3, D4, D5, Q0, Q1, Q2, Q3, Q4, Q5
  _74LS160 u_74ls160_1 (
    .ENP(1'b1), .ENT(1'b1), .nLOAD(1'b1), .D0(1'b0), .D1(1'b0), .D2(1'b0), .D3(1'b0), .CLK(not_3_out),
    .nCLR(not_2_out), .Q0(n74ls160_1_q0), .Q1(n74ls160_1_q1), .Q2(n74ls160_1_q2), .Q3(n74ls160_1_q3));  // open: RCO
  Clock clock_1 (.out(clock_1_out));
  Button button_2 (.out(button_2_out));
  and and_2 (and_2_out, F_REG_q7, control_unit_1_zf);
  not not_1 (not_1_out, or_5_out);
  CONTROL_UNIT control_unit_1 (
    .T0(n74ls160_1_q0), .T1(n74ls160_1_q1), .T2(n74ls160_1_q2), .T3(n74ls160_1_q3), .I0(INSTRUCTION_REG_q0),
    .I1(INSTRUCTION_REG_q1), .I2(INSTRUCTION_REG_q2), .I3(INSTRUCTION_REG_q3), .I4(INSTRUCTION_REG_q4),
    .I5(INSTRUCTION_REG_q5), .I6(INSTRUCTION_REG_q6), .I7(INSTRUCTION_REG_q7),
    .\ΣOUT (\control_unit_1_σout ), .ADD_nSUB(control_unit_1_add_nsub), .\ΣIN (\control_unit_1_σin ),
    .A_In(control_unit_1_a_in), .A_out(control_unit_1_a_out), .B_In(control_unit_1_b_in),
    .B_out(control_unit_1_b_out), .C_In(control_unit_1_c_in), .C_out(control_unit_1_c_out),
    .D_IN(control_unit_1_d_in), .D_out(control_unit_1_d_out), .RI(control_unit_1_ri), .RO(control_unit_1_ro),
    .MAR_In(control_unit_1_mar_in), .PCE(control_unit_1_pce), .PC_IN(control_unit_1_pc_in),
    .PC_OUT(control_unit_1_pc_out), .IR_IN(control_unit_1_ir_in), .IC_R(control_unit_1_ic_r),
    .HLT(control_unit_1_hlt), .CF(control_unit_1_cf), .ZF(control_unit_1_zf), .INC(control_unit_1_inc));  // open: out_36
  not not_2 (not_2_out, or_4_out);
  or or_4 (or_4_out, control_unit_1_ic_r, button_3_out);
  not not_3 (not_3_out, and_4_out);
  nand nand_1 (nand_1_out, clock_1_out, in_1);
  nand nand_2 (nand_2_out, in_1, in_1);
  nand nand_3 (nand_3_out, nand_2_out, or_1_out);
  or or_5 (or_5_out, or_7_out, or_10_out);
  and and_3 (and_3_out, and_4_out, \control_unit_1_σout );
  _74LS574 INSTRUCTION_REG (
    .D0(n74ls245_2_q0[0]), .D1(n74ls245_2_q0[1]), .D2(n74ls245_2_q0[2]), .D3(n74ls245_2_q0[3]),
    .D4(n74ls245_2_q4[4]), .D5(n74ls245_2_q4[5]), .D6(n74ls245_2_q4[6]), .D7(n74ls245_2_q4[7]), .nOE(1'b0),
    .Q0(INSTRUCTION_REG_q0), .Q1(INSTRUCTION_REG_q1), .Q2(INSTRUCTION_REG_q2), .Q3(INSTRUCTION_REG_q3),
    .Q4(INSTRUCTION_REG_q4), .Q5(INSTRUCTION_REG_q5), .Q6(INSTRUCTION_REG_q6), .Q7(INSTRUCTION_REG_q7),
    .CP(and_5_out));
  nand nand_4 (nand_4_out, nand_1_out, nand_3_out);
  and and_4 (and_4_out, nand_4_out, or_12_out);
  _74LS245 u_74ls245_1 (
    .D0(in_10), .D1(in_9), .D2(in_8), .D3(in_7), .D4(in_6), .D5(ADDRESS), .D6(in_4), .D7(in_3), .nOE(MODE),
    .Q0(n74ls245_1_q0[0]), .Q1(n74ls245_1_q0[1]), .Q2(n74ls245_1_q0[2]), .Q3(n74ls245_1_q0[3]),
    .Q4(n74ls245_1_q0[4]), .Q5(n74ls245_1_q0[5]), .Q6(n74ls245_1_q0[6]), .Q7(n74ls245_1_q0[7]));
  nand nand_5 (nand_5_out, MODE, control_unit_1_ro);
  or or_6 (or_6_out, \n74ls83_2_σ0 , \n74ls83_2_σ1 );
  or or_7 (or_7_out, or_6_out, or_8_out);
  or or_8 (or_8_out, \n74ls83_2_σ2 , \n74ls83_2_σ3 );
  or or_9 (or_9_out, \n74ls83_1_σ0 , \n74ls83_1_σ1 );
  or or_10 (or_10_out, or_9_out, or_11_out);
  or or_11 (or_11_out, \n74ls83_1_σ2 , \n74ls83_1_σ3 );
  nand nand_6 (nand_6_out, MODE, \control_unit_1_σout );
  xor xor_1 (xor_1_out, control_unit_1_add_nsub, \Σ_REG_q0 );
  not not_4 (not_4_out, 1'b0);
  not not_5 (not_5_out, nand_10_out);
  nand nand_7 (nand_7_out, control_unit_1_ri, and_4_out);
  nand nand_8 (nand_8_out, PGM_out, PGM_out);
  _74LS83 u_74ls83_1 (
    .A3(and_8_out), .B3(xor_1_out), .A2(and_9_out), .B2(xor_2_out), .A1(and_10_out), .B1(xor_3_out),
    .A0(and_11_out), .B0(xor_5_out), .C0(n74ls83_2_c4), .C4(n74ls83_1_c4), .\Σ3 (\n74ls83_1_σ3 ),
    .\Σ2 (\n74ls83_1_σ2 ), .\Σ1 (\n74ls83_1_σ1 ), .\Σ0 (\n74ls83_1_σ0 ));
  xor xor_2 (xor_2_out, control_unit_1_add_nsub, \Σ_REG_q1 );
  xor xor_3 (xor_3_out, control_unit_1_add_nsub, \Σ_REG_q2 );
  _74LS574 \u_Σ_REG  (
    .D0(n74ls245_2_q4[7]), .D1(n74ls245_2_q4[6]), .D2(n74ls245_2_q4[5]), .D3(n74ls245_2_q4[4]),
    .D4(n74ls245_2_q0[3]), .D5(n74ls245_2_q0[2]), .D6(n74ls245_2_q0[1]), .D7(n74ls245_2_q0[0]), .nOE(1'b0),
    .Q0(\Σ_REG_q0 ), .Q1(\Σ_REG_q1 ), .Q2(\Σ_REG_q2 ), .Q3(\Σ_REG_q3 ), .Q4(\Σ_REG_q4 ), .Q5(\Σ_REG_q5 ),
    .Q6(\Σ_REG_q6 ), .Q7(\Σ_REG_q7 ), .CP(and_7_out));
  not not_6 (not_6_out, control_unit_1_hlt);
  and and_5 (and_5_out, control_unit_1_ir_in, and_4_out);
  _74LS245 u_74ls245_2 (
    .D0(in_18), .D1(in_17), .D2(in_16), .D3(in_15), .D4(in_14), .D5(in_13), .D6(Data), .D7(in_11),
    .nOE(MODE), .Q0(n74ls245_2_q0[0]), .Q1(n74ls245_2_q0[1]), .Q2(n74ls245_2_q0[2]), .Q3(n74ls245_2_q0[3]),
    .Q4(n74ls245_2_q4[4]), .Q5(n74ls245_2_q4[5]), .Q6(n74ls245_2_q4[6]), .Q7(n74ls245_2_q4[7]));
  RAM #(.bus("separate")) ram_1 (
    .addr(n74ls245_1_q0), .din({n74ls245_2_q4, n74ls245_2_q0}), .data(ram_1_data), .str(1'b1),
    .sel(not_4_out), .clk(not_5_out), .ld(1'b1));  // open: clr
  assign {n74ls245_2_q4, n74ls245_2_q0} = not_7_out ? ram_1_data : 8'bz;  // Controlled_Buffer controlled_buffer_1
  not not_7 (not_7_out, nand_5_out);
  nand nand_9 (nand_9_out, nand_7_out, nand_8_out);
  nand nand_10 (nand_10_out, nand_9_out, nand_9_out);
  _74LS83 u_74ls83_2 (
    .A3(and_12_out), .B3(xor_4_out), .A2(and_13_out), .B2(xor_6_out), .A1(and_14_out), .B1(xor_7_out),
    .A0(or_13_out), .B0(xor_8_out), .C0(control_unit_1_add_nsub), .C4(n74ls83_2_c4), .\Σ3 (\n74ls83_2_σ3 ),
    .\Σ2 (\n74ls83_2_σ2 ), .\Σ1 (\n74ls83_2_σ1 ), .\Σ0 (\n74ls83_2_σ0 ));
  xor xor_4 (xor_4_out, control_unit_1_add_nsub, \Σ_REG_q4 );
  xor xor_5 (xor_5_out, control_unit_1_add_nsub, \Σ_REG_q3 );
  buf or_12 (or_12_out, not_6_out);  // OR_Gate
  Button PGM (.out(PGM_out));
  _74LS574 MAR (
    .D0(n74ls245_2_q0[0]), .D1(n74ls245_2_q0[1]), .D2(n74ls245_2_q0[2]), .D3(n74ls245_2_q0[3]),
    .D4(n74ls245_2_q4[4]), .D5(n74ls245_2_q4[5]), .D6(n74ls245_2_q4[6]), .D7(n74ls245_2_q4[7]),
    .nOE(not_8_out), .Q0(n74ls245_1_q0[0]), .Q1(n74ls245_1_q0[1]), .Q2(n74ls245_1_q0[2]),
    .Q3(n74ls245_1_q0[3]), .Q4(n74ls245_1_q0[4]), .Q5(n74ls245_1_q0[5]), .Q6(n74ls245_1_q0[6]),
    .Q7(n74ls245_1_q0[7]), .CP(and_6_out));
  and and_6 (and_6_out, control_unit_1_mar_in, and_4_out);
  xor xor_6 (xor_6_out, control_unit_1_add_nsub, \Σ_REG_q5 );
  xor xor_7 (xor_7_out, control_unit_1_add_nsub, \Σ_REG_q6 );
  and and_7 (and_7_out, \control_unit_1_σin , and_4_out);
  not not_8 (not_8_out, MODE);
  _74LS245 u_74ls245_3 (
    .D0(\n74ls83_2_σ0 ), .D1(\n74ls83_2_σ1 ), .D2(\n74ls83_2_σ2 ), .D3(\n74ls83_2_σ3 ), .D4(\n74ls83_1_σ0 ),
    .D5(\n74ls83_1_σ1 ), .D6(\n74ls83_1_σ2 ), .D7(\n74ls83_1_σ3 ), .nOE(nand_6_out), .Q0(n74ls245_2_q0[0]),
    .Q1(n74ls245_2_q0[1]), .Q2(n74ls245_2_q0[2]), .Q3(n74ls245_2_q0[3]), .Q4(n74ls245_2_q4[4]),
    .Q5(n74ls245_2_q4[5]), .Q6(n74ls245_2_q4[6]), .Q7(n74ls245_2_q4[7]));
  xor xor_8 (xor_8_out, control_unit_1_add_nsub, \Σ_REG_q7 );
  and and_8 (and_8_out, A_q7, not_9_out);
  and and_9 (and_9_out, A_q6, not_9_out);
  and and_10 (and_10_out, A_q5, not_9_out);
  and and_11 (and_11_out, A_q4, not_9_out);
  and and_12 (and_12_out, A_q3, not_9_out);
  and and_13 (and_13_out, A_q2, not_9_out);
  and and_14 (and_14_out, A_q1, not_9_out);
  or or_13 (or_13_out, A_q0, control_unit_1_inc);
  Hex_Digit_Display hex_digit_display_1 (.value(n74ls245_2_q4));  // open: dp
  Hex_Digit_Display hex_digit_display_2 (.value(n74ls245_2_q0));  // open: dp
  _74LS160 u_74ls160_2 (
    .ENP(control_unit_1_pce), .ENT(control_unit_1_pce), .nLOAD(nand_17_out), .D0(n74ls245_2_q0[0]),
    .D1(n74ls245_2_q0[1]), .D2(n74ls245_2_q0[2]), .D3(n74ls245_2_q0[3]), .CLK(and_4_out), .nCLR(nand_16_out),
    .Q0(n74ls160_2_q0), .Q1(n74ls160_2_q1), .Q2(n74ls160_2_q2), .Q3(n74ls160_2_q3), .RCO(n74ls160_2_rco));
  _74LS245 u_74ls245_4 (
    .D0(A_q0), .D1(A_q1), .D2(A_q2), .D3(A_q3), .D4(A_q4), .D5(A_q5), .D6(A_q6), .D7(A_q7),
    .nOE(nand_11_out), .Q0(n74ls245_2_q0[0]), .Q1(n74ls245_2_q0[1]), .Q2(n74ls245_2_q0[2]),
    .Q3(n74ls245_2_q0[3]), .Q4(n74ls245_2_q4[4]), .Q5(n74ls245_2_q4[5]), .Q6(n74ls245_2_q4[6]),
    .Q7(n74ls245_2_q4[7]));
  not not_9 (not_9_out, control_unit_1_inc);
  _74LS574 A (
    .D0(n74ls245_2_q0[0]), .D1(n74ls245_2_q0[1]), .D2(n74ls245_2_q0[2]), .D3(n74ls245_2_q0[3]),
    .D4(n74ls245_2_q4[4]), .D5(n74ls245_2_q4[5]), .D6(n74ls245_2_q4[6]), .D7(n74ls245_2_q4[7]), .nOE(1'b0),
    .Q0(A_q0), .Q1(A_q1), .Q2(A_q2), .Q3(A_q3), .Q4(A_q4), .Q5(A_q5), .Q6(A_q6), .Q7(A_q7), .CP(and_15_out));
  _74LS574 B (
    .D0(n74ls245_2_q0[0]), .D1(n74ls245_2_q0[1]), .D2(n74ls245_2_q0[2]), .D3(n74ls245_2_q0[3]),
    .D4(n74ls245_2_q4[4]), .D5(n74ls245_2_q4[5]), .D6(n74ls245_2_q4[6]), .D7(n74ls245_2_q4[7]),
    .nOE(nand_12_out), .Q0(n74ls245_2_q0[0]), .Q1(n74ls245_2_q0[1]), .Q2(n74ls245_2_q0[2]),
    .Q3(n74ls245_2_q0[3]), .Q4(n74ls245_2_q4[4]), .Q5(n74ls245_2_q4[5]), .Q6(n74ls245_2_q4[6]),
    .Q7(n74ls245_2_q4[7]), .CP(and_16_out));
  _74LS574 C (
    .D0(n74ls245_2_q0[0]), .D1(n74ls245_2_q0[1]), .D2(n74ls245_2_q0[2]), .D3(n74ls245_2_q0[3]),
    .D4(n74ls245_2_q4[4]), .D5(n74ls245_2_q4[5]), .D6(n74ls245_2_q4[6]), .D7(n74ls245_2_q4[7]),
    .nOE(nand_13_out), .Q0(n74ls245_2_q0[0]), .Q1(n74ls245_2_q0[1]), .Q2(n74ls245_2_q0[2]),
    .Q3(n74ls245_2_q0[3]), .Q4(n74ls245_2_q4[4]), .Q5(n74ls245_2_q4[5]), .Q6(n74ls245_2_q4[6]),
    .Q7(n74ls245_2_q4[7]), .CP(and_17_out));
  _74LS574 D (
    .D0(n74ls245_2_q0[0]), .D1(n74ls245_2_q0[1]), .D2(n74ls245_2_q0[2]), .D3(n74ls245_2_q0[3]),
    .D4(n74ls245_2_q4[4]), .D5(n74ls245_2_q4[5]), .D6(n74ls245_2_q4[6]), .D7(n74ls245_2_q4[7]),
    .nOE(nand_14_out), .Q0(n74ls245_2_q0[0]), .Q1(n74ls245_2_q0[1]), .Q2(n74ls245_2_q0[2]),
    .Q3(n74ls245_2_q0[3]), .Q4(n74ls245_2_q4[4]), .Q5(n74ls245_2_q4[5]), .Q6(n74ls245_2_q4[6]),
    .Q7(n74ls245_2_q4[7]), .CP(and_18_out));
  Hex_Digit_Display hex_digit_display_3 (.value(n74ls245_2_q0));  // open: dp
  Hex_Digit_Display hex_digit_display_4 (.value(n74ls245_2_q4));  // open: dp
  _74LS245 u_74ls245_5 (
    .D0(n74ls160_2_q0), .D1(n74ls160_2_q1), .D2(n74ls160_2_q2), .D3(n74ls160_2_q3), .D4(n74ls160_3_q0),
    .D5(n74ls160_3_q1), .D6(n74ls160_3_q2), .D7(n74ls160_3_q3), .nOE(nand_15_out), .Q0(n74ls245_2_q0[0]),
    .Q1(n74ls245_2_q0[1]), .Q2(n74ls245_2_q0[2]), .Q3(n74ls245_2_q0[3]), .Q4(n74ls245_2_q4[4]),
    .Q5(n74ls245_2_q4[5]), .Q6(n74ls245_2_q4[6]), .Q7(n74ls245_2_q4[7]));
  _74LS160 u_74ls160_3 (
    .ENP(n74ls160_2_rco), .ENT(control_unit_1_pce), .nLOAD(nand_17_out), .D0(n74ls245_2_q4[4]),
    .D1(n74ls245_2_q4[5]), .D2(n74ls245_2_q4[6]), .D3(n74ls245_2_q4[7]), .CLK(and_4_out), .nCLR(nand_16_out),
    .Q0(n74ls160_3_q0), .Q1(n74ls160_3_q1), .Q2(n74ls160_3_q2), .Q3(n74ls160_3_q3));  // open: RCO
  and and_15 (and_15_out, and_4_out, control_unit_1_a_in);
  nand nand_11 (nand_11_out, control_unit_1_a_out, MODE);
  and and_16 (and_16_out, and_4_out, control_unit_1_b_in);
  nand nand_12 (nand_12_out, control_unit_1_b_out, MODE);
  and and_17 (and_17_out, and_4_out, control_unit_1_c_in);
  nand nand_13 (nand_13_out, control_unit_1_c_out, MODE);
  and and_18 (and_18_out, and_4_out, control_unit_1_d_in);
  nand nand_14 (nand_14_out, control_unit_1_d_out, MODE);
  nand nand_15 (nand_15_out, control_unit_1_pc_out, MODE);
  SSD ssd_1 (
    .D7(A_q7), .D6(A_q6), .D5(A_q5), .D4(A_q4), .D3(A_q3), .D2(A_q2), .D1(A_q1), .D0(A_q0),
    .DISP3(ssd_1_disp3), .DISP2(ssd_1_disp2), .DISP1(ssd_1_disp1));
  nand nand_16 (nand_16_out, button_3_out, button_3_out);
  nand nand_17 (nand_17_out, or_2_out, or_2_out);
  Hex_Digit_Display hex_digit_display_5 (.value(ssd_1_disp3));  // open: dp
  Button button_3 (.out(button_3_out));
  Hex_Digit_Display hex_digit_display_6 (.value(ssd_1_disp1));  // open: dp
  Hex_Digit_Display hex_digit_display_7 (.value(ssd_1_disp2));  // open: dp

  assign BUS_HLD_IP = MODE;

  // Notes on the sheet:
  //   ALU
  //   MASTER CLOCK
  //   INSTRUCTION DECODE AND CONTROL UNIT
  //   256bytes RAM
  //   Data Bus
  //   Data Bus
  //   PROGRAM COUNTER
endmodule

// DM74LS574
module _74LS574 (
  input  D0,
  input  D1,
  input  D2,
  input  D3,
  input  D4,
  input  D5,
  input  D6,
  input  D7,
  input  nOE,
  input  CP,
  output Q0,
  output Q1,
  output Q2,
  output Q3,
  output Q4,
  output Q5,
  output Q6,
  output Q7
);

  wire d_ff_1_q, d_ff_2_q, d_ff_3_q, d_ff_4_q, d_ff_5_q, d_ff_6_q, d_ff_7_q, d_ff_8_q, not_1_out;

  not not_1 (not_1_out, nOE);
  D_Flip_Flop d_ff_1 (.clk(CP), .D(D0), .Q(d_ff_1_q));  // open: Qn, preset, en, reset
  D_Flip_Flop d_ff_2 (.clk(CP), .D(D1), .Q(d_ff_2_q));  // open: Qn, preset, en, reset
  D_Flip_Flop d_ff_3 (.clk(CP), .D(D2), .Q(d_ff_3_q));  // open: Qn, preset, en, reset
  D_Flip_Flop d_ff_4 (.clk(CP), .D(D3), .Q(d_ff_4_q));  // open: Qn, preset, en, reset
  D_Flip_Flop d_ff_5 (.clk(CP), .D(D4), .Q(d_ff_5_q));  // open: Qn, preset, en, reset
  D_Flip_Flop d_ff_6 (.clk(CP), .D(D5), .Q(d_ff_6_q));  // open: Qn, preset, en, reset
  D_Flip_Flop d_ff_7 (.clk(CP), .D(D6), .Q(d_ff_7_q));  // open: Qn, preset, en, reset
  D_Flip_Flop d_ff_8 (.clk(CP), .D(D7), .Q(d_ff_8_q));  // open: Qn, preset, en, reset
  assign Q0 = not_1_out ? d_ff_1_q : 1'bz;  // Controlled_Buffer controlled_buffer_1
  assign Q1 = not_1_out ? d_ff_2_q : 1'bz;  // Controlled_Buffer controlled_buffer_2
  assign Q2 = not_1_out ? d_ff_3_q : 1'bz;  // Controlled_Buffer controlled_buffer_3
  assign Q3 = not_1_out ? d_ff_4_q : 1'bz;  // Controlled_Buffer controlled_buffer_4
  assign Q4 = not_1_out ? d_ff_5_q : 1'bz;  // Controlled_Buffer controlled_buffer_5
  assign Q5 = not_1_out ? d_ff_6_q : 1'bz;  // Controlled_Buffer controlled_buffer_6
  assign Q6 = not_1_out ? d_ff_7_q : 1'bz;  // Controlled_Buffer controlled_buffer_7
  assign Q7 = not_1_out ? d_ff_8_q : 1'bz;  // Controlled_Buffer controlled_buffer_8
endmodule

// DM74LS245
module _74LS245 (
  input  D0,
  input  D1,
  input  D2,
  input  D3,
  input  D4,
  input  D5,
  input  D6,
  input  D7,
  input  nOE,
  output Q0,
  output Q1,
  output Q2,
  output Q3,
  output Q4,
  output Q5,
  output Q6,
  output Q7
);

  wire not_1_out;

  not not_1 (not_1_out, nOE);
  assign Q0 = not_1_out ? D0 : 1'bz;  // Controlled_Buffer controlled_buffer_1
  assign Q1 = not_1_out ? D1 : 1'bz;  // Controlled_Buffer controlled_buffer_2
  assign Q2 = not_1_out ? D2 : 1'bz;  // Controlled_Buffer controlled_buffer_3
  assign Q3 = not_1_out ? D3 : 1'bz;  // Controlled_Buffer controlled_buffer_4
  assign Q4 = not_1_out ? D4 : 1'bz;  // Controlled_Buffer controlled_buffer_5
  assign Q5 = not_1_out ? D5 : 1'bz;  // Controlled_Buffer controlled_buffer_6
  assign Q6 = not_1_out ? D6 : 1'bz;  // Controlled_Buffer controlled_buffer_7
  assign Q7 = not_1_out ? D7 : 1'bz;  // Controlled_Buffer controlled_buffer_8
endmodule

// DM74LS83
module _74LS83 (
  input  A3,
  input  B3,
  input  A2,
  input  B2,
  input  A1,
  input  B1,
  input  A0,
  input  B0,
  input  C0,
  output C4,
  output \Σ3 ,
  output \Σ2 ,
  output \Σ1 ,
  output \Σ0 
);

  wire and_1_out, and_2_out, and_3_out, and_4_out, and_5_out, and_6_out, and_7_out, and_8_out, and_9_out,
       and_10_out, and_11_out, and_12_out, and_13_out, and_14_out, buffer_1_out, buffer_2_out, buffer_3_out,
       buffer_4_out, nand_1_out, nand_2_out, nand_3_out, nand_4_out, nor_1_out, nor_2_out, nor_3_out,
       nor_4_out, nor_6_out, nor_7_out, nor_8_out, not_1_out, not_2_out, not_3_out, not_4_out, not_5_out,
       not_6_out;

  not not_1 (not_1_out, C0);
  nand nand_1 (nand_1_out, A3, B3);
  nor nor_1 (nor_1_out, A3, B3);
  nand nand_2 (nand_2_out, A2, B2);
  nor nor_2 (nor_2_out, A2, B2);
  nand nand_3 (nand_3_out, A1, B1);
  nor nor_3 (nor_3_out, A1, B1);
  nand nand_4 (nand_4_out, A0, B0);
  nor nor_4 (nor_4_out, A0, B0);
  buf buffer_1 (buffer_1_out, nor_1_out);
  not not_2 (not_2_out, nor_1_out);
  buf buffer_2 (buffer_2_out, nor_2_out);
  not not_3 (not_3_out, nor_2_out);
  buf buffer_3 (buffer_3_out, nor_3_out);
  not not_4 (not_4_out, nor_3_out);
  buf buffer_4 (buffer_4_out, nor_4_out);
  not not_5 (not_5_out, nor_4_out);
  not not_6 (not_6_out, not_1_out);
  and and_1 (and_1_out, nor_2_out, nand_1_out);
  and and_2 (and_2_out, nor_3_out, nand_1_out, nand_2_out);
  and and_3 (and_3_out, nor_4_out, nand_1_out, nand_2_out, nand_3_out);
  and and_4 (and_4_out, nand_1_out, nand_2_out, nand_3_out, nand_4_out, not_1_out);
  and and_5 (and_5_out, nand_1_out, not_2_out);
  and and_6 (and_6_out, nor_3_out, nand_2_out);
  and and_7 (and_7_out, nand_2_out, nor_4_out, nand_3_out);
  and and_8 (and_8_out, nand_2_out, nand_3_out, nand_4_out, not_1_out);
  and and_9 (and_9_out, nand_2_out, not_3_out);
  and and_10 (and_10_out, nor_4_out, nand_3_out);
  and and_11 (and_11_out, nand_3_out, nand_4_out, not_1_out);
  and and_12 (and_12_out, nand_3_out, not_4_out);
  and and_13 (and_13_out, nand_4_out, not_1_out);
  and and_14 (and_14_out, nand_4_out, not_5_out);
  nor nor_5 (C4, buffer_1_out, and_1_out, and_2_out, and_3_out, and_4_out);
  xor xor_1 (\Σ3 , and_5_out, nor_6_out);
  nor nor_6 (nor_6_out, buffer_2_out, and_6_out, and_7_out, and_8_out);
  xor xor_2 (\Σ2 , and_9_out, nor_7_out);
  nor nor_7 (nor_7_out, buffer_3_out, and_10_out, and_11_out);
  xor xor_3 (\Σ1 , and_12_out, nor_8_out);
  nor nor_8 (nor_8_out, buffer_4_out, and_13_out);
  xor xor_4 (\Σ0 , and_14_out, not_6_out);
endmodule

module CONTROL_UNIT (
  input  T0,
  input  T1,
  input  T2,
  input  T3,
  input  I0,
  input  I1,
  input  I2,
  input  I3,
  input  I4,
  input  I5,
  input  I6,
  input  I7,
  output \ΣOUT ,
  output ADD_nSUB,
  output \ΣIN ,
  output A_In,
  output A_out,
  output B_In,
  output B_out,
  output C_In,
  output C_out,
  output D_IN,
  output D_out,
  output RI,
  output RO,
  output MAR_In,
  output PCE,
  output PC_IN,
  output PC_OUT,
  output IR_IN,
  output IC_R,
  output HLT,
  output CF,
  output ZF,
  output INC,
  output out_36
);

  Hex_Digit_Display hex_digit_display_1 (.value({T3, T2, T1, T0}));  // open: dp
  ROM #(.addrWidth(12)) rom_1 (
    .addr({I7, I6, I5, I4, I3, I2, I1, I0, T3, T2, T1, T0}),
    .data({\ΣOUT , ADD_nSUB, \ΣIN , A_In, A_out, B_In, B_out, C_In}));  // open: sel
  ROM #(.addrWidth(12)) rom_2 (
    .addr({I7, I6, I5, I4, I3, I2, I1, I0, T3, T2, T1, T0}),
    .data({C_out, D_IN, D_out, RI, RO, MAR_In, PCE, PC_IN}));  // open: sel
  ROM #(.addrWidth(12)) rom_3 (
    .addr({I7, I6, I5, I4, I3, I2, I1, I0, T3, T2, T1, T0}),
    .data({PC_OUT, IR_IN, IC_R, HLT, CF, ZF, INC, out_36}));  // open: sel

  // Notes on the sheet:
  //   contents of rom_1 (hex, n*v repeats v):
  //   20*0 10 15*0 8 14*0 10 16*0 20 90 30*0 20 d0 13*0 20 90 14*0 20 d0 45*0 2 10 15*0 10 15*0 10 14*0 2
  //   8 15*0 8 15*0 8 15*0 4 15*0 1 30*0 c 15*0 9 15*0 8 15*0 12 15*0 3 15*0 2 15*0 10 15*0 4 31*0 10 15*0
  //   4 15*0 1 15*0 28 90 14*0 22 90 14*0 20 90 14*0 20 90 14*0 28 d0 14*0 22 d0 14*0 20 d0 14*0 20 d0
  //   14*0 28 90 14*0 22 84 14*0 20 81 14*0 20 80
  //   contents of rom_2 (hex, n*v repeats v):
  //   6 8 14*0 6 8 6 c 8 11*0 6 8 6 c 10 11*0 6 8 6 8 12*0 6 8 6 c 8 11*0 6 8 6 9 12*0 6 8 6 c 8 11*0 6 8
  //   6 8 12*0 6 8 6 8 12*0 6 8 6 8 12*0 6 8 6 8 12*0 6 8 4 8 12*0 6 8 84 8 12*0 6 8 24 8 12*0 6 8 4 10
  //   12*0 6 8 84 10 12*0 6 8 24 10 12*0 6 8 6 8 12*0 6 8 6 8 12*0 6 8 6 48 12*0 6 8 14*0 6 8 14*0 6 8 40
  //   13*0 6 8 14*0 6 8 14*0 6 8 40 13*0 6 8 80 13*0 6 8 80 13*0 6 8 c0 13*0 6 8 20 13*0 6 8 20 13*0 6 8
  //   20 13*0 6 8 14*0 6 8 14*0 6 8 80 13*0 6 8 20 13*0 6 8 14*0 6 8 14*0 6 8 80 13*0 6 8 20 13*0 6 8 14*0
  //   6 8 14*0 6 8 80 13*0 6 8 20 40 12*0 6 8 14*0 6 8 14*0 6 8 14*0 6 8 14*0 6 8 14*0 6 8 14*0 6 8 14*0 6
  //   8 14*0 6 8 14*0 6 8 14*0 6 8 14*0 6 8 14*0 6 8 14*0 6 8 14*0 6 8 14*0 6 8 14*0 6 8 14*0 6 8 14*0 6 8
  //   14*0 6 8 3070*0 6 8
  //   contents of rom_3 (hex, n*v repeats v):
  //   80 40 20 13*0 80 40 80 0 0 20 10*0 80 40 80 0 0 20 10*0 80 40 80 0 20 11*0 80 40 80 0 0 0 20 9*0 80
  //   40 80 0 20 11*0 80 40 80 0 0 0 20 9*0 80 40 80 0 0 20 10*0 80 40 80 0 0 20 10*0 80 40 80 4 20 11*0
  //   80 40 80 8 20 11*0 80 40 0 0 20 11*0 80 40 0 0 20 11*0 80 40 0 0 20 11*0 80 40 0 0 20 11*0 80 40 0 0
  //   20 11*0 80 40 0 0 20 11*0 80 40 80 0 20 11*0 80 40 80 0 20 11*0 80 40 80 0 20 11*0 80 40 0 20 12*0
  //   80 40 0 20 12*0 80 40 0 20 12*0 80 40 0 20 12*0 80 40 0 20 12*0 80 40 0 20 12*0 80 40 0 20 12*0 80
  //   40 0 20 12*0 80 40 0 20 12*0 80 40 0 20 12*0 80 40 0 20 12*0 80 40 0 20 12*0 80 40 0 0 20 11*0 80 40
  //   0 0 20 11*0 80 40 0 0 20 11*0 80 40 0 0 20 11*0 80 40 0 0 20 11*0 80 40 0 0 20 11*0 80 40 0 0 20
  //   11*0 80 40 0 0 20 11*0 80 40 0 2 20 11*0 80 40 0 2 20 11*0 80 40 0 2 20 11*0 80 40 0 2 20 11*0 80 40
  //   14*0 80 40 14*0 80 40 14*0 80 40 14*0 80 40 14*0 80 40 14*0 80 40 14*0 80 40 14*0 80 40 14*0 80 40
  //   14*0 80 40 14*0 80 40 14*0 80 40 14*0 80 40 14*0 80 40 14*0 80 40 14*0 80 40 14*0 80 40 14*0 80 40
  //   14*0 80 40 3070*0 80 40 10
endmodule

// 74LS161
module _74LS160 (
  input  ENP,
  input  ENT,
  input  nLOAD,
  input  D0,
  input  D1,
  input  D2,
  input  D3,
  input  CLK,
  input  nCLR,
  output Q0,
  output Q1,
  output Q2,
  output Q3,
  output RCO
);

  wire and_1_out, not_1_out, not_2_out;

  and and_1 (and_1_out, ENP, nLOAD, ENT);
  not not_1 (not_1_out, nLOAD);
  not not_2 (not_2_out, nCLR);
  Counter #(.width(4), .max('hf)) counter_1 (
    .load(not_1_out), .D({D3, D2, D1, D0}), .count(and_1_out), .Q({Q3, Q2, Q1, Q0}), .carry(RCO), .clk(CLK),
    .clr(not_2_out));
endmodule

module SSD (
  input  D7,
  input  D6,
  input  D5,
  input  D4,
  input  D3,
  input  D2,
  input  D1,
  input  D0,
  output [3:0] DISP3,
  output [3:0] DISP2,
  output [3:0] DISP1
);

  ROM #(.dataWidth(4)) rom_1 (.addr({D7, D6, D5, D4, D3, D2, D1, D0}), .data(DISP3));  // open: sel
  ROM #(.dataWidth(4)) rom_2 (.addr({D7, D6, D5, D4, D3, D2, D1, D0}), .data(DISP2));  // open: sel
  ROM #(.dataWidth(4)) rom_3 (.addr({D7, D6, D5, D4, D3, D2, D1, D0}), .data(DISP1));  // open: sel
  Hex_Digit_Display hex_digit_display_1 (.value(DISP3));  // open: dp
  Hex_Digit_Display hex_digit_display_2 (.value(DISP1));  // open: dp
  Hex_Digit_Display hex_digit_display_3 (.value(DISP2));  // open: dp

  // Notes on the sheet:
  //   contents of rom_1 (hex, n*v repeats v):
  //   100*0 100*1 56*2
  //   contents of rom_2 (hex, n*v repeats v):
  //   10*0 10*1 10*2 10*3 10*4 10*5 10*6 10*7 10*8 10*9 10*0 10*1 10*2 10*3 10*4 10*5 10*6 10*7 10*8 10*9
  //   10*0 10*1 10*2 10*3 10*4 6*5
  //   contents of rom_3 (hex, n*v repeats v):
  //   0 1 2 3 4 5 6 7 8 9 0 1 2 3 4 5 6 7 8 9 0 1 2 3 4 5 6 7 8 9 0 1 2 3 4 5 6 7 8 9 0 1 2 3 4 5 6 7 8 9
  //   0 1 2 3 4 5 6 7 8 9 0 1 2 3 4 5 6 7 8 9 0 1 2 3 4 5 6 7 8 9 0 1 2 3 4 5 6 7 8 9 0 1 2 3 4 5 6 7 8 9
  //   0 1 2 3 4 5 6 7 8 9 0 1 2 3 4 5 6 7 8 9 0 1 2 3 4 5 6 7 8 9 0 1 2 3 4 5 6 7 8 9 0 1 2 3 4 5 6 7 8 9
  //   0 1 2 3 4 5 6 7 8 9 0 1 2 3 4 5 6 7 8 9 0 1 2 3 4 5 6 7 8 9 0 1 2 3 4 5 6 7 8 9 0 1 2 3 4 5 6 7 8 9
  //   0 1 2 3 4 5 6 7 8 9 0 1 2 3 4 5 6 7 8 9 0 1 2 3 4 5 6 7 8 9 0 1 2 3 4 5 6 7 8 9 0 1 2 3 4 5 6 7 8 9
  //   0 1 2 3 4 5
endmodule
